// Logisim project ALU_8_bit.circ as structural Verilog: 8 circuits, main circuit ALU
module ALU (
  input  [3:0] Opcode,
  input  Enable,
  input  [7:0] A,
  input  [7:0] B,
  output [7:0] C,
  output [3:0] Flags
);

  wire and_1_out, and_2_out, and_3_out, math_1_carryout, nor_1_out, not_1_out, not_2_out, rotate_1_carryout;
  wire [7:0] logic_1_c, math_1_c, multiplexer_1_out, multiplexer_2_out, rotate_1_c;

  and and_1 (and_1_out, Opcode[2], Opcode[3]);
  Multiplexer #(.width(8)) multiplexer_1 (.in0(B), .in1(8'h1), .out(multiplexer_1_out), .sel(and_1_out));
  and and_2 (and_2_out, Opcode[2], Opcode[1], Opcode[0]);
  not not_1 (not_1_out, and_2_out);
  Math math_1 (
    .Carry(Opcode[0]), .Negate(Opcode[1]), .B(A), .A(multiplexer_1_out), .C(math_1_c),
    .CarryOut(math_1_carryout));
  Logic logic_1 (.data1(Opcode[0]), .data2(Opcode[1]), .A(A), .B(multiplexer_1_out), .C(logic_1_c));
  Rotate rotate_1 (.left_right(Opcode[0]), .carry(Opcode[1]), .A(A), .C(rotate_1_c), .carryOut(rotate_1_carryout));
  and and_3 (and_3_out, not_1_out, Enable);
  assign C = and_3_out ? multiplexer_2_out : 8'bz;  // Controlled_Buffer controlled_buffer_1
  Multiplexer #(.select(2), .width(8)) multiplexer_2 (
    .in0(math_1_c), .in1(logic_1_c), .in2(rotate_1_c), .in3(math_1_c), .out(multiplexer_2_out),
    .sel(Opcode[3:2]));
  nor nor_1 (nor_1_out, multiplexer_2_out[1], multiplexer_2_out[2], multiplexer_2_out[3], multiplexer_2_out[4], multiplexer_2_out[5], multiplexer_2_out[6], multiplexer_2_out[7]);
  Multiplexer #(.select(2)) multiplexer_3 (
    .in0(math_1_carryout), .in1(1'b0), .in2(rotate_1_carryout), .in3(1'b0), .out(Flags[3]), .sel(Opcode[3:2]));
  not not_2 (not_2_out, multiplexer_2_out[0]);
  and and_4 (Flags[2], not_2_out, nor_1_out);
  and and_5 (Flags[1], nor_1_out, multiplexer_2_out[0]);
  not not_3 (Flags[0], multiplexer_2_out[0]);

  // Notes on the sheet:
  //   Carry
  //   Zero
  //   One
  //   Even
endmodule

module full_ADD_SUB_one_bit (
  input  A,
  input  B,
  input  C,
  input  Negate,
  output O,
  output Carry
);

  wire and_1_out, and_2_out, and_3_out, xor_1_out, xor_2_out;

  xor xor_1 (xor_1_out, Negate, A);
  xor xor_2 (xor_2_out, A, B);
  xor xor_3 (O, xor_2_out, C);
  and and_1 (and_1_out, B, C);
  and and_2 (and_2_out, C, xor_1_out);
  and and_3 (and_3_out, B, xor_1_out);
  or or_1 (Carry, and_1_out, and_2_out, and_3_out);

  // Notes on the sheet:
  //   N = 0 : A+B+C
  //   N = 1 : A-B-C
endmodule

module Math (
  input  Carry,
  input  Negate,
  input  [7:0] B,
  input  [7:0] A,
  output [7:0] C,
  output CarryOut
);

  wire full_add_sub_one_bit_1_carry, full_add_sub_one_bit_2_carry, full_add_sub_one_bit_3_carry,
       full_add_sub_one_bit_4_carry, full_add_sub_one_bit_5_carry, full_add_sub_one_bit_6_carry,
       full_add_sub_one_bit_7_carry;

  full_ADD_SUB_one_bit full_add_sub_one_bit_1 (
    .A(B[0]), .B(A[0]), .C(Carry), .Negate(Negate), .O(C[0]), .Carry(full_add_sub_one_bit_1_carry));
  full_ADD_SUB_one_bit full_add_sub_one_bit_2 (
    .A(B[1]), .B(A[1]), .C(full_add_sub_one_bit_1_carry), .Negate(Negate), .O(C[1]),
    .Carry(full_add_sub_one_bit_2_carry));
  full_ADD_SUB_one_bit full_add_sub_one_bit_3 (
    .A(B[2]), .B(A[2]), .C(full_add_sub_one_bit_2_carry), .Negate(Negate), .O(C[2]),
    .Carry(full_add_sub_one_bit_3_carry));
  full_ADD_SUB_one_bit full_add_sub_one_bit_4 (
    .A(B[3]), .B(A[3]), .C(full_add_sub_one_bit_3_carry), .Negate(Negate), .O(C[3]),
    .Carry(full_add_sub_one_bit_4_carry));
  full_ADD_SUB_one_bit full_add_sub_one_bit_5 (
    .A(B[4]), .B(A[4]), .C(full_add_sub_one_bit_4_carry), .Negate(Negate), .O(C[4]),
    .Carry(full_add_sub_one_bit_5_carry));
  full_ADD_SUB_one_bit full_add_sub_one_bit_6 (
    .A(B[5]), .B(A[5]), .C(full_add_sub_one_bit_5_carry), .Negate(Negate), .O(C[5]),
    .Carry(full_add_sub_one_bit_6_carry));
  full_ADD_SUB_one_bit full_add_sub_one_bit_7 (
    .A(B[6]), .B(A[6]), .C(full_add_sub_one_bit_6_carry), .Negate(Negate), .O(C[6]),
    .Carry(full_add_sub_one_bit_7_carry));
  full_ADD_SUB_one_bit full_add_sub_one_bit_8 (
    .A(B[7]), .B(A[7]), .C(full_add_sub_one_bit_7_carry), .Negate(Negate), .O(C[7]), .Carry(CarryOut));
endmodule

module Rotate (
  input  left_right,
  input  carry,
  input  [7:0] A,
  output [7:0] C,
  output carryOut
);

  Multiplexer #(.width(8)) multiplexer_1 (.in0({A[6:0], carry}), .in1({carry, A[7:1]}), .out(C), .sel(left_right));
  Multiplexer multiplexer_2 (.in0(A[7]), .in1(A[0]), .out(carryOut), .sel(left_right));

  // Notes on the sheet:
  //   data1 = left or right // data2 = with or without carry
endmodule

module Logic (
  input  data1,
  input  data2,
  input  [7:0] A,
  input  [7:0] B,
  output [7:0] C
);

  wire [7:0] and_1_out, or_1_out, xor_1_out;

  assign and_1_out = A & B;  // AND_Gate and_1, 8 bits wide
  assign xor_1_out = A ^ B;  // XOR_Gate xor_1, 8 bits wide
  assign or_1_out = A | B;  // OR_Gate or_1, 8 bits wide
  Multiplexer #(.select(2), .width(8)) multiplexer_1 (
    .in0(and_1_out), .in1(xor_1_out), .in2(or_1_out), .out(C), .sel({data2, data1}));  // open: in3
endmodule

module Registers (
  input  Clock,
  input  Reset,
  input  [7:0] D_In,
  input  Red_Enable,
  input  Write_Enable,
  input  [2:0] Addr_reg_Out,
  input  [2:0] Addr_reg_In,
  input  Arith_Ope,
  input  Addr_Select,
  output [7:0] D_Out,
  output [15:0] Addr_Out
);

  wire decoder_1_out0, decoder_1_out1, decoder_1_out2, decoder_1_out3, decoder_1_out4, decoder_1_out5,
       decoder_1_out6, xor_1_out, xor_2_out;
  wire [2:0] pull_resistor_1_node, pull_resistor_2_node;
  wire [7:0] A_q, B_q, C_q, D_q, E_q, H_q, L_q;

  Decoder #(.select(3)) decoder_1 (
    .out0(decoder_1_out0), .out1(decoder_1_out1), .out2(decoder_1_out2), .out3(decoder_1_out3),
    .out4(decoder_1_out4), .out5(decoder_1_out5), .out6(decoder_1_out6), .sel(pull_resistor_1_node),
    .en(Write_Enable));  // open: out7
  Pull_Resistor pull_resistor_1 (.node(pull_resistor_1_node));
  assign pull_resistor_1_node = xor_1_out ? Addr_reg_In : 3'bz;  // Controlled_Buffer controlled_buffer_1
  xor xor_1 (xor_1_out, Write_Enable, Arith_Ope);
  Register A (.D(D_In), .en(decoder_1_out0), .Q(A_q), .clk(Clock), .clr(Reset));
  Register B (.D(D_In), .en(decoder_1_out1), .Q(B_q), .clk(Clock), .clr(Reset));
  Register C (.D(D_In), .en(decoder_1_out2), .Q(C_q), .clk(Clock), .clr(Reset));
  Register D (.D(D_In), .en(decoder_1_out3), .Q(D_q), .clk(Clock), .clr(Reset));
  Register E (.D(D_In), .en(decoder_1_out4), .Q(E_q), .clk(Clock), .clr(Reset));
  Register H (.D(D_In), .en(decoder_1_out5), .Q(H_q), .clk(Clock), .clr(Reset));
  Register L (.D(D_In), .en(decoder_1_out6), .Q(L_q), .clk(Clock), .clr(Reset));
  assign Addr_Out = Addr_Select ? {H_q, L_q} : 16'bz;  // Controlled_Buffer controlled_buffer_2
  Multiplexer #(.enable("true"), .select(3), .width(8)) multiplexer_1 (
    .in0(A_q), .in1(B_q), .in2(C_q), .in3(D_q), .in4(E_q), .in5(H_q), .in6(L_q), .out(D_Out),
    .sel(pull_resistor_2_node), .en(Red_Enable));  // open: in7
  Pull_Resistor pull_resistor_2 (.node(pull_resistor_2_node));
  assign pull_resistor_2_node = xor_2_out ? Addr_reg_Out : 3'bz;  // Controlled_Buffer controlled_buffer_3
  xor xor_2 (xor_2_out, Red_Enable, Arith_Ope);
endmodule

module Main (
);

  ALU alu_1 ();  // open: Opcode, Enable, A, B, C, Flags
  Registers registers_1 ();  // open: Clock, Reset, D_In, Red_Enable, Write_Enable, Addr_reg_Out, Addr_reg_In, Arith_Ope, Addr_Select, D_Out, Addr_Out
  Data_Stack data_stack_1 ();  // open: Pop, Push, Clock, Data_In, Data_Out
endmodule

module Data_Stack (
  input  Pop,
  input  Push,
  input  Clock,
  input  [7:0] Data_In,
  output [7:0] Data_Out
);

  wire not_1_out, xnor_1_out, xor_1_out;
  wire [7:0] counter_1_q, multiplexer_1_out, pull_resistor_1_node;

  xor xor_1 (xor_1_out, Pop, Push);
  Counter counter_1 (.count(xor_1_out), .Q(counter_1_q), .up(Push), .clk(Clock));  // open: load, D, carry, clr
  xnor xnor_1 (xnor_1_out, Push, Clock);
  Pull_Resistor pull_resistor_1 (.node(pull_resistor_1_node));
  RAM #(.readbehav("war")) ram_1 (
    .addr(counter_1_q), .we(xor_1_out), .oe(not_1_out), .clk(xnor_1_out), .din(multiplexer_1_out),
    .dout(Data_Out));
  not not_1 (not_1_out, Push);
  Multiplexer #(.width(8)) multiplexer_1 (
    .in0(pull_resistor_1_node), .in1(Data_In), .out(multiplexer_1_out), .sel(Push));
endmodule
